# Fritzing sketch a01-secondary-serial-hookup (saved by Fritzing 0.9.3b)

parts:
  U2 = NodeMCU V1.0
  Part3 = FTDI Basic Programmer

nets:
  GND: U2.D1, U2.TX, U2.GND, Part3.RXI, Part3.GND

notes:
  Testing of NodeMCU Entering Boot Loader Mode
  NodeMCU 1.0
  Secondary
  USB to serial
  converter

custom parts:
  NodeMCU V1.0: ESP8266 based NodeMCU V1.0
